# Fritzing sketch Kartenleser_Fotomodul (saved by Fritzing 0.9.3b)
circuit board: 2cm x 8.6cm
breadboards: 1

parts:
  R1 = Resistor [tolerance=±0.1% resistance=330 power=250mW package="1206 [SMD]"]
  R5 = Resistor [tolerance=±0.1% resistance=330 power=250mW package="1206 [SMD]"]
  R3 = Resistor [tolerance=±0.1% resistance=330 power=250mW package="1206 [SMD]"]
  R2 = Resistor [tolerance=±0.1% resistance=330 power=250mW package="1206 [SMD]"]
  R4 = Resistor [tolerance=±0.1% resistance=330 power=250mW package="1206 [SMD]"]
  F1 = PHOTOCELL [package=photocell]
  F2 = PHOTOCELL [package=photocell]
  F3 = PHOTOCELL [package=photocell]
  F4 = PHOTOCELL [package=photocell]
  F5 = PHOTOCELL [package=photocell]
  FM = Generic female header - 7 pins [form="♀ (female)" package=THT]
  LM = Generic female header - 2 pins [form="♀ (female)" package=THT]
  Connector = female pin header, 6 pins [form="♀ (female)"]  # not connected

nets:
  N1: R1.Pin_0, F1.P$2, FM.pin3
  N2: R1.Pin_1, R5.Pin_1, R3.Pin_1, R2.Pin_1, R4.Pin_1, FM.pin2, LM.pin2
  N3: R5.Pin_0, F5.P$2, FM.pin7
  N4: R3.Pin_0, F3.P$2, FM.pin5
  N5: R2.Pin_0, F2.P$2, FM.pin4
  N6: R4.Pin_0, F4.P$2, FM.pin6
  N7: F1.P$1, F2.P$1, F3.P$1, F4.P$1, F5.P$1, FM.pin1, LM.pin1

custom parts:
  Generic female header - 7 pins: Generic female header
  Generic female header - 2 pins: Generic female header
