# Fritzing sketch Kartenleser_Lichtmodul (saved by Fritzing 0.9.2b)
circuit board: 2cm x 7cm
breadboards: 1

parts:
  LED1 = LED - 3mm [color="White (4500K)" part_number=D-3mm current=20mA package="3 mm [THT]"]
  LED2 = LED - 3mm [color="White (4500K)" part_number=D-3mm current=20mA package="3 mm [THT]"]
  LED3 = LED - 3mm [color="White (4500K)" part_number=D-3mm current=20mA package="3 mm [THT]"]
  LED4 = LED - 3mm [color="White (4500K)" part_number=D-3mm current=20mA package="3 mm [THT]"]
  LED5 = LED - 3mm [color="White (4500K)" part_number=D-3mm current=20mA package="3 mm [THT]"]
  R1 = Resistor [tolerance=±0.1% resistance=330 power=250mW package="1206 [SMD]"]
  R4 = Resistor [tolerance=±0.1% resistance=330 power=250mW package="1206 [SMD]"]
  R5 = Resistor [tolerance=±0.1% resistance=330 power=250mW package="1206 [SMD]"]
  R3 = Resistor [tolerance=±0.1% resistance=330 power=250mW package="1206 [SMD]"]
  R2 = Resistor [tolerance=±0.1% resistance=330 power=250mW package="1206 [SMD]"]
  LM = Generic female header - 2 pins [form="♀ (female)" package=THT]

nets:
  N1: LED1.cathode, LED2.cathode, LED3.cathode, LED4.cathode, LED5.cathode, LM.pin2
  N2: LED1.anode, R1.Pin_0
  N3: LED2.anode, R2.Pin_0
  N4: LED3.anode, R3.Pin_0
  N5: LED4.anode, R4.Pin_0
  N6: LED5.anode, R5.Pin_0
  N7: R1.Pin_1, R4.Pin_1, R5.Pin_1, R3.Pin_1, R2.Pin_1, LM.pin1

custom parts:
  Generic female header - 2 pins: Generic female header
