# Fritzing sketch Displaymodul (saved by Fritzing 0.9.3b)
circuit board: 3.31693cm x 5.41783cm
breadboards: 1

parts:
  Summer = Buzzer 12mm [package=buzzer-12mm-ns]
  Displaymodul = 7 Segment Display
  R3 = Resistor [tolerance=±5% resistance=330 package="1206 [SMD]"]
  R4 = Resistor [tolerance=±5% resistance=330 package="1206 [SMD]"]
  R5 = Resistor [tolerance=±5% resistance=330 power=0.25W package="1206 [SMD]"]
  R1 = Resistor [tolerance=±5% resistance=330 package="1206 [SMD]"]
  R7 = Resistor [tolerance=±5% resistance=330 package="1206 [SMD]"]
  R2 = Resistor [tolerance=±5% resistance=330 package="1206 [SMD]"]
  U1 = 74HC595 SMD [package="SO16 [SMD]"]
  Display = female pin header, 6 pins [form="♀ (female)"]
  R8 = Resistor [tolerance=±5% resistance=330 package="1206 [SMD]"]
  R6 = Resistor [tolerance=±5% resistance=330 package="1206 [SMD]"]

nets:
  N1: Summer.1, Display.pin6
  N2: Summer.2, Displaymodul.common_anode#11, Displaymodul.common_anode#16, U1.GND, U1.OE, Display.pin2
  N3: Displaymodul.Segment_A, R8.Pin_0
  N4: Displaymodul.Segment_F, R3.Pin_0
  N5: Displaymodul.Segment_E, R2.Pin_0
  N6: Displaymodul.Segment_DP, R5.Pin_0
  N7: Displaymodul.Segment_D, R6.Pin_0
  N8: Displaymodul.common_anode#12, R1.Pin_0
  N9: Displaymodul.Segment_G, R4.Pin_0
  N10: Displaymodul.Segment_B, R7.Pin_0
  N11: R3.Pin_1, U1.Q5
  N12: R4.Pin_1, U1.Q6
  N13: R5.Pin_1, U1.Q7
  N14: R1.Pin_1, U1.Q2
  N15: R7.Pin_1, U1.Q1
  N16: R2.Pin_1, U1.Q4
  N17: U1.Q3, R6.Pin_1
  N18: U1.MR, U1.VCC, Display.pin1
  N19: U1.SH_CP, Display.pin5
  N20: U1.ST_CP, Display.pin4
  N21: U1.DS, Display.pin3
  N22: U1.Q0, R8.Pin_1
