# Fritzing sketch BoomBalloon-Wiring (saved by Fritzing 0.9.3b)
circuit board: 4.73169cm x 6.70196cm
breadboards: 1

parts:
  R2 = Resistor [tolerance=±5% resistance=2.2k power=0.5W part_number=BF0411 package=THT]
  Motor = Basic FET N-Channel [package="TO220 [THT]"]
  D1 = Rectifier Diode [part_number=1N4004 package="300 mil [THT]"]
  D2 = Rectifier Diode [part_number=1N4004 package="300 mil [THT]"]
  R1 = Resistor [tolerance=±5% resistance=2.2k power=0.5W part_number=BF0411 package=THT]
  MA = female pin header, 1 pin [form="♀ (female)"]
  VA = female pin header, 1 pin [form="♀ (female)"]
  VM = female pin header, 1 pin [form="♀ (female)"]
  MM = female pin header, 1 pin [form="♀ (female)"]
  Fotomodul = female pin header, 7 pins [form="♀ (female)"]
  Displaymodul = female pin header, 6 pins [form="♀ (female)"]
  Direkt2 = female pin header, 6 pins [form="♀ (female)"]
  Direkt3 = female pin header, 5 pins [form="♀ (female)"]
  Direkt1 = female pin header, 1 pin [form="♀ (female)"]
  Direkt4 = female pin header, 1 pin [form="♀ (female)"]
  Direkt5 = female pin header, 1 pin [form="♀ (female)"]
  Direkt6 = female pin header, 1 pin [form="♀ (female)"]
  Direkt7 = female pin header, 3 pins [form="♀ (female)"]
  Direkt8 = female pin header, 2 pins [form="♀ (female)"]
  Vcc_12V = female pin header, 2 pins [form="♀ (female)"]
  Direkt10 = female pin header, 1 pin [form="♀ (female)"]
  Direkt11 = female pin header, 1 pin [form="♀ (female)"]
  Bauteil2 = Arduino Micro (Rev3)
  Ablassmotor = Basic FET N-Channel [package="TO220 [THT]"]
  Direkt12 = female pin header, 1 pin [form="♀ (female)"]
  Direkt13 = female pin header, 1 pin [form="♀ (female)"]
  Power_Jack = Power Jack [package=power_jack_pth]  # not connected

nets:
  N1: R2.Pin_0, Ablassmotor.gate
  N2: R2.Pin_1, Direkt8.pin1
  N3: Motor.gate, R1.Pin_0
  N4: Motor.drain, D2.anode, MM.pin1
  N5: Motor.source, Fotomodul.pin2, Displaymodul.pin2, Vcc_12V.pin2, Direkt10.pin1, Direkt11.pin1, Bauteil2.GND, Ablassmotor.source
  N6: D1.cathode, D2.cathode, VA.pin1, VM.pin1, Direkt7.pin1, Vcc_12V.pin1, Bauteil2.VIN
  N7: D1.anode, MA.pin1, Ablassmotor.drain
  N8: R1.Pin_1, Direkt8.pin2
  N9: Fotomodul.pin1, Bauteil2.3V3, Direkt13.pin1
  N10: Fotomodul.pin3, Bauteil2.A0
  N11: Fotomodul.pin4, Bauteil2.A1
  N12: Fotomodul.pin5, Bauteil2.A2
  N13: Fotomodul.pin6, Bauteil2.A3
  N14: Fotomodul.pin7, Bauteil2.A4
  N15: Displaymodul.pin1, Bauteil2.5V, Direkt12.pin1
  N16: Displaymodul.pin3, Bauteil2.D8_PWM/A8
  N17: Displaymodul.pin4, Bauteil2.D9_PWM/A9
  N18: Displaymodul.pin5, Bauteil2.D10_PWM/A10
  N19: Displaymodul.pin6, Bauteil2.D11_PWM
  N20: Direkt2.pin1, Bauteil2.D7
  N21: Direkt2.pin2, Bauteil2.D6_PWM/A7
  N22: Direkt2.pin3, Bauteil2.D5_PWM
  N23: Direkt2.pin4, Bauteil2.D4_PWM/A6
  N24: Direkt2.pin5, Bauteil2.D3/SCL
  N25: Direkt2.pin6, Bauteil2.D2/SDA
  N26: Direkt3.pin1, Bauteil2.RESET
  N27: Direkt3.pin2, Bauteil2.D0/RX
  N28: Direkt3.pin3, Bauteil2.D1/TX
  N29: Direkt3.pin4, Bauteil2.RXLED/SS
  N30: Direkt3.pin5, Bauteil2.MOSI
  N31: Direkt1.pin1, Bauteil2.D12_PWM/A11
  N32: Direkt4.pin1, Bauteil2.D13_PWM
  N33: Direkt5.pin1, Bauteil2.AREF
  N34: Direkt6.pin1, Bauteil2.A5
  N35: Direkt7.pin2, Bauteil2.MISO
  N36: Direkt7.pin3, Bauteil2.SCK
